# Fritzing sketch projeto concluido (saved by Fritzing 0.9.3b)
breadboards: 1

parts:
  U1 = atmega328 [package=dip]
  DFRobot_DFPlayer_Mini1 = DFRobot DFPlayer Mini [part_number=DFR0299]
  Mod1 = KY-031 Knock Sensor Module [package="Breakout board"]
  SW-1 = Vibration sensor module
  LED1 = LEDs [package=led10mm]
  S1 = Square Pushbutton
  XTAL1 = Crystal [frequency="16 Mhz" package=THT]
  C1 = Capacitor [part_number=100pf package=cap-pth-small2]
  C2 = Capacitor [part_number=100pf package=cap-pth-small2]
  SP1 = SPEAKER [package=pcb_mount_speaker]
  R1 = Resistor [tolerance=±5% resistance=10k package="2010 [SMD]"]
  C3 = Ceramic Capacitor [capacitance=100nF package="100 mil [THT, multilayer]"]
  BAT1 = Battery Holders [package=lipo-1100mAh]

nets:
  N1: U1.RESET, R1.Pin_1, C3.1
  VCC: U1.VCC, U1.AVCC, DFRobot_DFPlayer_Mini1.VCC, Mod1.Vin, SW-1.vcc, S1.leg0, R1.Pin_0
  N2: U1.GND, DFRobot_DFPlayer_Mini1.GND-1, DFRobot_DFPlayer_Mini1.GND-2, Mod1.-, SW-1.Ground, LED1.C, C1.2, C2.1, C3.0, BAT1.-
  N3: U1.XLAT1, XTAL1.pin_0, C2.2
  N4: U1.XLAT2, XTAL1.pin_1, C1.1
  N5: U1.D6_(PWM), LED1.A
  N6: U1.D8, Mod1.S
  N7: U1.D9_(PWM), SW-1.Digital_output
  N8: U1.D10_(PWM), DFRobot_DFPlayer_Mini1.TX
  N9: U1.D11_(PWM), DFRobot_DFPlayer_Mini1.RX
  N10: DFRobot_DFPlayer_Mini1.SPK_1, SP1.-
  N11: DFRobot_DFPlayer_Mini1.SPK_2, SP1.+
  N12: S1.leg1, BAT1.+

custom parts:
  KY-031 Knock Sensor Module: KY-031 Knock Sensor module. A vibration sensor that sends a signal when a knock/tap is detected.
  Vibration sensor module: Single-roller type full induction trigger switch. When no vibration or tilt, the product is ON conduction state, and in the steady state, when a vibration or tilt, the switch will be rendered instantly disconnect the conductive resistance increases, generating a current pulse signal, thereby triggering circuit. The default state of the swith is close Digital output Supply voltage:3.3V-5V On-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
