# Fritzing sketch projeto na placa de circuito (saved by Fritzing 0.9.3b)
perfboards: 1

parts:
  U1 = atmega328 [package=dip]
  C1 = Ceramic Capacitor [capacitance=100nF package="100 mil [THT, multilayer]"]  # not connected
  C2 = Capacitor [package=cap-pth-small2]
  C3 = Capacitor [package=cap-pth-small2]
  XTAL1 = Crystal [frequency="16 Mhz" package=THT]
  DFRobot_DFPlayer_Mini1 = DFRobot DFPlayer Mini [part_number=DFR0299]
  Mod1 = KY-031 Knock Sensor Module [package="Breakout board"]
  SW-1 = Vibration sensor module
  R2 = Resistor [tolerance=±5% resistance=10k package="2010 [SMD]"]
  LED2 = LEDs [package=led10mm]
  SP2 = SPEAKER [package=pcb_mount_speaker]
  BAT2 = Battery Holders [package=lipo-1100mAh]
  S2 = Square Pushbutton

nets:
  N1: U1.RESET, R2.Pin_1
  N2: U1.GND, C3.2, DFRobot_DFPlayer_Mini1.GND-1, DFRobot_DFPlayer_Mini1.GND-2, Mod1.-, SW-1.Ground
  N3: U1.XLAT1, C3.1, XTAL1.pin_0
  N4: U1.XLAT2, C2.1, XTAL1.pin_1
  N5: U1.D6_(PWM), LED2.A
  N6: U1.D8, Mod1.S
  N7: U1.D9_(PWM), SW-1.Digital_output
  VCC: U1.AVCC, DFRobot_DFPlayer_Mini1.VCC, Mod1.Vin, R2.Pin_0
  N8: DFRobot_DFPlayer_Mini1.SPK_1, SP2.-
  N9: DFRobot_DFPlayer_Mini1.SPK_2, SP2.+
  N10: BAT2.+, S2.leg1

custom parts:
  KY-031 Knock Sensor Module: KY-031 Knock Sensor module. A vibration sensor that sends a signal when a knock/tap is detected.
  Vibration sensor module: Single-roller type full induction trigger switch. When no vibration or tilt, the product is ON conduction state, and in the steady state, when a vibration or tilt, the switch will be rendered instantly disconnect the conductive resistance increases, generating a current pulse signal, thereby triggering circuit. The default state of the swith is close Digital output Supply voltage:3.3V-5V On-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
